# Fritzing sketch 4-1 (saved by Fritzing 0.9.4)
breadboards: 1

parts:
  LED1 = LED - 5mm [color="Red (633nm)" package="5 mm [THT]"]
  R1 = Resistor [tolerance=±5% resistance=220 package=THT]
  Part1 = Arduino Uno (Rev3)

nets:
  N1: LED1.cathode, Part1.D9_PWM
  N2: LED1.anode, R1.Pin_0
  N3: R1.Pin_1, Part1.GND
