# Fritzing sketch 4-5 (saved by Fritzing 0.9.4)
breadboards: 1

parts:
  Part1 = Arduino Uno (Rev3)
  U1 = POT [package=pot_mammoth]
  U2 = LCD-16X2 [package=lcd-16x2]

nets:
  N1: Part1.D11_PWM/MOSI, U2.E
  N2: Part1.D12/MISO, U2.RS
  N3: Part1.D2, U2.DB7
  N4: Part1.D3_PWM, U2.DB6
  N5: Part1.D4, U2.DB5
  N6: Part1.D5_PWM, U2.DB4
  5V: Part1.5V, U1.E, U2.VDD, U2.A
  GND: Part1.GND, U1.S, U2.VSS, U2.R_W, U2.K
  N7: U1.A, U2.VO
