# Fritzing sketch 4-6 (saved by Fritzing 0.9.4)
breadboards: 1

parts:
  Part1 = Arduino Uno (Rev3)
  U1 = POT [package=pot_mammoth]
  U2 = LCD-16X2 [package=lcd-16x2]
  HC-SR04_Sensor_1 = HC-SR04 Ultrasonic Distance Sensor

nets:
  N1: Part1.D9_PWM, HC-SR04_Sensor_1.TRIG
  N2: Part1.D10_PWM/SS, HC-SR04_Sensor_1.ECHO
  N3: Part1.D11_PWM/MOSI, U2.E
  N4: Part1.D12/MISO, U2.RS
  N5: Part1.D2, U2.DB7
  N6: Part1.D3_PWM, U2.DB6
  N7: Part1.D4, U2.DB5
  N8: Part1.D5_PWM, U2.DB4
  5V: Part1.5V, U1.E, U2.VDD, U2.A, HC-SR04_Sensor_1.VCC
  GND: Part1.GND, U1.S, U2.VSS, U2.R_W, U2.K, HC-SR04_Sensor_1.GND
  N9: U1.A, U2.VO
