# Fritzing sketch 4-7 (saved by Fritzing 0.9.4)
breadboards: 1

parts:
  HC-SR04_Sensor_1 = HC-SR04 Ultrasonic Distance Sensor
  R1 = Resistor [tolerance=±5% resistance=220 package=THT]
  LED1 = LED - 5mm [color="Red (633nm)" package="5 mm [THT]"]
  Part1 = Arduino Uno (Rev3)

nets:
  VCC: HC-SR04_Sensor_1.VCC, Part1.5V
  N1: HC-SR04_Sensor_1.TRIG, Part1.D9_PWM
  N2: HC-SR04_Sensor_1.ECHO, Part1.D10_PWM/SS
  GND: HC-SR04_Sensor_1.GND, R1.Pin_1, Part1.GND
  N3: R1.Pin_0, LED1.anode
  N4: LED1.cathode, Part1.D11_PWM/MOSI
